// Logisim project projet_Processeur.circ as structural Verilog: 28 circuits, main circuit main
module main (
  input  WE_RAM,
  input  OE_RAM,
  input  WE,
  input  [2:0] right,
  output [7:0] res,
  output erreur
);

  wire [2:0] decodeur_1_op, decodeur_1_rin1, decodeur_1_rin2, decodeur_1_typeope;
  wire [7:0] bancregistre_1_memoire1, bancregistre_1_memoire2, bancregistre_1_memoire3,
       bancregistre_1_memoire4, bancregistre_1_memoire5, bancregistre_1_memoire6, bancregistre_1_memoire7,
       bancregistre_1_memoire8, load_1_reg_in, multiplexer_1_out, multiplexer_2_out, ramdonnees_1_sortie;
  wire [23:0] chemindonnees_1_out_1;

  Clock infoClock ();  // open: out
  RAMdonnees ramdonnees_1 (
    .adresse(multiplexer_1_out), .WE(WE_RAM), .OE(OE_RAM), .sortie(ramdonnees_1_sortie));  // open: entre
  CheminDonnees chemindonnees_1 (.out_1(chemindonnees_1_out_1));
  LOAD load_1 (.ALU(res), .RAM(ramdonnees_1_sortie), .REG_IN(load_1_reg_in));  // open: CNST8, instruction
  decodeur decodeur_1 (
    .instruction(chemindonnees_1_out_1), .typeOpe(decodeur_1_typeope), .OP(decodeur_1_op),
    .Rin1(decodeur_1_rin1), .Rin2(decodeur_1_rin2), .Rout(right));  // open: Void
  BancRegistre bancregistre_1 (
    .Value(load_1_reg_in), .WE(WE), .right(right), .memoire1(bancregistre_1_memoire1),
    .memoire2(bancregistre_1_memoire2), .memoire3(bancregistre_1_memoire3),
    .memoire4(bancregistre_1_memoire4), .memoire5(bancregistre_1_memoire5),
    .memoire6(bancregistre_1_memoire6), .memoire7(bancregistre_1_memoire7), .memoire8(bancregistre_1_memoire8));
  Multiplexer #(.select(3), .width(8)) multiplexer_1 (
    .in0(bancregistre_1_memoire1), .in1(bancregistre_1_memoire2), .in2(bancregistre_1_memoire3),
    .in3(bancregistre_1_memoire4), .in4(bancregistre_1_memoire5), .in5(bancregistre_1_memoire6),
    .in6(bancregistre_1_memoire7), .in7(bancregistre_1_memoire8), .out(multiplexer_1_out),
    .sel(decodeur_1_rin1));
  Multiplexer #(.select(3), .width(8)) multiplexer_2 (
    .in0(bancregistre_1_memoire1), .in1(bancregistre_1_memoire2), .in2(bancregistre_1_memoire3),
    .in3(bancregistre_1_memoire4), .in4(bancregistre_1_memoire5), .in5(bancregistre_1_memoire6),
    .in6(bancregistre_1_memoire7), .in7(bancregistre_1_memoire8), .out(multiplexer_2_out),
    .sel(decodeur_1_rin2));
  UAL ual_1 (
    .A(multiplexer_1_out), .B(multiplexer_2_out), .typeOpe(decodeur_1_typeope[1:0]), .ope(decodeur_1_op),
    .res(res), .erreur(erreur));
endmodule

module add1bit (
  input  A,
  input  B,
  input  R,
  output res,
  output res_R
);

  wire and_1_out, and_2_out, and_3_out, or_1_out, xor_1_out;

  xor xor_1 (xor_1_out, A, B);
  and and_1 (and_1_out, A, B);
  and and_2 (and_2_out, R, A);
  and and_3 (and_3_out, R, B);
  xor xor_2 (res, xor_1_out, R);
  or or_1 (or_1_out, and_2_out, and_3_out);
  or or_2 (res_R, and_1_out, or_1_out);
endmodule

module add (
  input  [7:0] A,
  input  [7:0] B,
  output [7:0] res,
  output overflow
);

  wire add1bit_1_res_r, add1bit_2_res_r, add1bit_3_res_r, add1bit_4_res_r, add1bit_5_res_r, add1bit_6_res_r,
       add1bit_7_res_r;

  add1bit add1bit_1 (.A(A[0]), .B(B[0]), .R(1'b0), .res(res[0]), .res_R(add1bit_1_res_r));
  add1bit add1bit_2 (.A(A[1]), .B(B[1]), .R(add1bit_1_res_r), .res(res[1]), .res_R(add1bit_2_res_r));
  add1bit add1bit_3 (.A(A[2]), .B(B[2]), .R(add1bit_2_res_r), .res(res[2]), .res_R(add1bit_3_res_r));
  add1bit add1bit_4 (.A(A[3]), .B(B[3]), .R(add1bit_3_res_r), .res(res[3]), .res_R(add1bit_4_res_r));
  add1bit add1bit_5 (.A(A[4]), .B(B[4]), .R(add1bit_4_res_r), .res(res[4]), .res_R(add1bit_5_res_r));
  add1bit add1bit_6 (.A(A[5]), .B(B[5]), .R(add1bit_5_res_r), .res(res[5]), .res_R(add1bit_6_res_r));
  add1bit add1bit_7 (.A(A[6]), .B(B[6]), .R(add1bit_6_res_r), .res(res[6]), .res_R(add1bit_7_res_r));
  add1bit add1bit_8 (.A(A[7]), .B(B[7]), .R(add1bit_7_res_r), .res(res[7]), .res_R(overflow));
endmodule

module sub (
  input  [7:0] A,
  input  [7:0] B,
  output [7:0] res,
  output erreur
);

  wire add_1_overflow, add_2_overflow;
  wire [7:0] add_1_res, not_1_out;

  assign not_1_out = ~B;  // NOT_Gate not_1, 8 bits wide
  add add_1 (.A(not_1_out), .B(8'h1), .res(add_1_res), .overflow(add_1_overflow));
  // NoConnect on add_1_overflow
  add add_2 (.A(A), .B(add_1_res), .res(res), .overflow(add_2_overflow));
  // NoConnect on add_2_overflow

  assign erreur = B[7];
endmodule

module and8bit (
  input  [7:0] A,
  input  [7:0] B,
  output [7:0] res
);

  assign res = A & B;  // AND_Gate and_1, 8 bits wide
endmodule

module or8bit (
  input  [7:0] A,
  input  [7:0] B,
  output [7:0] res
);

  assign res = A | B;  // OR_Gate or_1, 8 bits wide
endmodule

module xor8bit (
  input  [7:0] A,
  input  [7:0] B,
  output [7:0] res
);

  assign res = A ^ B;  // XOR_Gate xor_1, 8 bits wide
endmodule

module Equal (
  input  [7:0] A,
  input  [7:0] B,
  output res
);

  wire [7:0] not_1_out, xor_1_out;

  assign xor_1_out = A ^ B;  // XOR_Gate xor_1, 8 bits wide
  assign not_1_out = ~xor_1_out;  // NOT_Gate not_1, 8 bits wide
  and and_1 (res, not_1_out[0], not_1_out[1], not_1_out[2], not_1_out[3], not_1_out[4], not_1_out[5], not_1_out[6], not_1_out[7]);
endmodule

module diff (
  input  [7:0] A,
  input  [7:0] B,
  output res
);

  wire equal_1_res;

  Equal equal_1 (.A(A), .B(B), .res(equal_1_res));
  not not_1 (res, equal_1_res);
endmodule

module inf1bit (
  input  suivant,
  input  A,
  input  B,
  output res,
  output \continue 
);

  wire and_1_out, not_1_out, not_2_out, xor_1_out;

  not not_1 (not_1_out, A);
  and and_1 (and_1_out, not_1_out, B);
  xor xor_1 (xor_1_out, A, B);
  not not_2 (not_2_out, xor_1_out);
  and and_2 (res, and_1_out, suivant);
  and and_3 (\continue , suivant, not_2_out);
endmodule

module inf (
  input  [7:0] A,
  input  [7:0] B,
  output res
);

  wire inf1bit_1_continue, inf1bit_1_res, inf1bit_2_continue, inf1bit_2_res, inf1bit_3_continue,
       inf1bit_3_res, inf1bit_4_continue, inf1bit_4_res, inf1bit_5_continue, inf1bit_5_res,
       inf1bit_6_continue, inf1bit_6_res, inf1bit_7_continue, inf1bit_7_res, inf1bit_8_continue,
       inf1bit_8_res;

  inf1bit inf1bit_1 (.suivant(1'b1), .A(A[7]), .B(B[7]), .res(inf1bit_1_res), .\continue (inf1bit_1_continue));
  inf1bit inf1bit_2 (
    .suivant(inf1bit_1_continue), .A(A[6]), .B(B[6]), .res(inf1bit_2_res), .\continue (inf1bit_2_continue));
  inf1bit inf1bit_3 (
    .suivant(inf1bit_2_continue), .A(A[5]), .B(B[5]), .res(inf1bit_3_res), .\continue (inf1bit_3_continue));
  inf1bit inf1bit_4 (
    .suivant(inf1bit_3_continue), .A(A[4]), .B(B[4]), .res(inf1bit_4_res), .\continue (inf1bit_4_continue));
  inf1bit inf1bit_5 (
    .suivant(inf1bit_4_continue), .A(A[3]), .B(B[3]), .res(inf1bit_5_res), .\continue (inf1bit_5_continue));
  inf1bit inf1bit_6 (
    .suivant(inf1bit_5_continue), .A(A[2]), .B(B[2]), .res(inf1bit_6_res), .\continue (inf1bit_6_continue));
  inf1bit inf1bit_7 (
    .suivant(inf1bit_6_continue), .A(A[1]), .B(B[1]), .res(inf1bit_7_res), .\continue (inf1bit_7_continue));
  inf1bit inf1bit_8 (
    .suivant(inf1bit_7_continue), .A(A[0]), .B(B[0]), .res(inf1bit_8_res), .\continue (inf1bit_8_continue));
  // NoConnect on inf1bit_8_continue
  or or_1 (res, inf1bit_1_res, inf1bit_2_res, inf1bit_3_res, inf1bit_4_res, inf1bit_5_res, inf1bit_6_res, inf1bit_7_res, inf1bit_8_res);
endmodule

module sup (
  input  [7:0] A,
  input  [7:0] B,
  output res
);

  wire equal_1_res, inf_1_res, not_1_out, not_2_out;

  not not_1 (not_1_out, inf_1_res);
  inf inf_1 (.A(A), .B(B), .res(inf_1_res));
  not not_2 (not_2_out, equal_1_res);
  Equal equal_1 (.A(A), .B(B), .res(equal_1_res));
  and and_1 (res, not_1_out, not_2_out);
endmodule

module LSL (
  input  [7:0] A,
  output [7:0] res
);


  assign res = {A[6:0], 1'b0};
endmodule

module BlocArithmetiques (
  input  [7:0] A,
  input  [7:0] B,
  input  ope,
  output [7:0] res,
  output erreur
);

  wire add_1_overflow, sub_1_erreur;
  wire [7:0] add_1_res, sub_1_res;

  add add_1 (.A(A), .B(B), .res(add_1_res), .overflow(add_1_overflow));
  sub sub_1 (.A(A), .B(B), .res(sub_1_res), .erreur(sub_1_erreur));
  Multiplexer #(.width(8)) multiplexer_1 (.in0(add_1_res), .in1(sub_1_res), .out(res), .sel(ope));
  Multiplexer multiplexer_2 (.in0(add_1_overflow), .in1(sub_1_erreur), .out(erreur), .sel(ope));
endmodule

module BlocLogiques (
  input  [7:0] A,
  input  [7:0] B,
  input  [1:0] ope,
  output [7:0] res
);

  wire [7:0] and8bit_1_res, or8bit_1_res, undriven, xor8bit_1_res;

  and8bit and8bit_1 (.A(A), .B(B), .res(and8bit_1_res));
  or8bit or8bit_1 (.A(A), .B(B), .res(or8bit_1_res));
  xor8bit xor8bit_1 (.A(A), .B(B), .res(xor8bit_1_res));
  Multiplexer #(.select(2), .width(8)) multiplexer_1 (
    .in0(and8bit_1_res), .in1(or8bit_1_res), .in2(xor8bit_1_res), .in3(undriven), .out(res), .sel(ope));
endmodule

module BlocComparaisons (
  input  [7:0] A,
  input  [7:0] B,
  input  [2:0] ope,
  output res
);

  wire diff_1_res, equal_1_res, inf_1_res, sup_1_res;

  inf inf_1 (.A(A), .B(B), .res(inf_1_res));
  Equal equal_1 (.A(A), .B(B), .res(equal_1_res));
  sup sup_1 (.A(A), .B(B), .res(sup_1_res));
  diff diff_1 (.A(A), .B(B), .res(diff_1_res));
  Multiplexer #(.select(3)) multiplexer_1 (
    .in1(inf_1_res), .in3(equal_1_res), .in5(sup_1_res), .in6(diff_1_res), .out(res), .sel(ope));  // open: in0, in2, in4, in7
endmodule

module BlocLSL (
  input  [7:0] A,
  input  [7:0] B,
  input  ope,
  output [7:0] res
);

  wire [7:0] lsl_1_res, undriven;

  LSL lsl_1 (.A(A), .res(lsl_1_res));
  Multiplexer #(.width(8)) multiplexer_1 (.in0(undriven), .in1(lsl_1_res), .out(res), .sel(ope));
endmodule

module UAL (
  input  [7:0] A,
  input  [7:0] B,
  input  [1:0] typeOpe,
  input  [2:0] ope,
  output [7:0] res,
  output erreur
);

  wire bloccomparaisons_1_res;
  wire [7:0] bit_extender_1_out, blocarithmetiques_1_res, bloclogiques_1_res, bloclsl_1_res;

  // NoConnect on ope[2]
  BlocArithmetiques blocarithmetiques_1 (.A(A), .B(B), .ope(ope[0]), .res(blocarithmetiques_1_res), .erreur(erreur));
  BlocLogiques bloclogiques_1 (.A(A), .B(B), .ope(ope[1:0]), .res(bloclogiques_1_res));
  BlocComparaisons bloccomparaisons_1 (.A(A), .B(B), .ope(ope), .res(bloccomparaisons_1_res));
  BlocLSL bloclsl_1 (.A(A), .B(B), .ope(ope[0]), .res(bloclsl_1_res));
  assign bit_extender_1_out = {{7{1'b0}}, bloccomparaisons_1_res};  // Bit_Extender bit_extender_1
  Multiplexer #(.select(2), .width(8)) multiplexer_1 (
    .in0(bit_extender_1_out), .in1(bloclsl_1_res), .in2(bloclogiques_1_res), .in3(blocarithmetiques_1_res),
    .out(res), .sel(typeOpe));
endmodule

module Registre1bit (
  input  [7:0] D,
  input  WE,
  output [7:0] out_3
);

  wire clock_1_out, d_ff_1_q;
  wire [7:0] multiplexer_1_out;

  Clock clock_1 (.out(clock_1_out));
  Multiplexer #(.width(8)) multiplexer_1 (.in0(out_3), .in1(D), .out(multiplexer_1_out), .sel(WE));
  D_Flip_Flop d_ff_1 (.D(multiplexer_1_out[0]), .clk(clock_1_out), .Q(d_ff_1_q));  // open: Qn, preset, reset
  assign out_3 = {{7{1'b0}}, d_ff_1_q};  // Bit_Extender bit_extender_1
endmodule

module Registre8bit (
  input  [7:0] D,
  input  WE,
  output [7:0] out_3
);

  wire clock_1_out;
  wire [7:0] multiplexer_1_out;

  Multiplexer #(.width(8)) multiplexer_1 (.in0(out_3), .in1(D), .out(multiplexer_1_out), .sel(WE));
  Clock clock_1 (.out(clock_1_out));
  D_Flip_Flop d_ff_1 (.D(multiplexer_1_out[0]), .clk(clock_1_out), .Q(out_3[0]));  // open: Qn, preset, reset
  D_Flip_Flop d_ff_2 (.D(multiplexer_1_out[1]), .clk(clock_1_out), .Q(out_3[1]));  // open: Qn, preset, reset
  D_Flip_Flop d_ff_3 (.D(multiplexer_1_out[2]), .clk(clock_1_out), .Q(out_3[2]));  // open: Qn, preset, reset
  D_Flip_Flop d_ff_4 (.D(multiplexer_1_out[3]), .clk(clock_1_out), .Q(out_3[3]));  // open: Qn, preset, reset
  D_Flip_Flop d_ff_5 (.D(multiplexer_1_out[4]), .clk(clock_1_out), .Q(out_3[4]));  // open: Qn, preset, reset
  D_Flip_Flop d_ff_6 (.D(multiplexer_1_out[5]), .clk(clock_1_out), .Q(out_3[5]));  // open: Qn, preset, reset
  D_Flip_Flop d_ff_7 (.D(multiplexer_1_out[6]), .clk(clock_1_out), .Q(out_3[6]));  // open: Qn, preset, reset
  D_Flip_Flop d_ff_8 (.D(multiplexer_1_out[7]), .clk(clock_1_out), .Q(out_3[7]));  // open: Qn, preset, reset
endmodule

module BancRegistre (
  input  [7:0] Value,
  input  WE,
  input  [2:0] right,
  output [7:0] memoire1,
  output [7:0] memoire2,
  output [7:0] memoire3,
  output [7:0] memoire4,
  output [7:0] memoire5,
  output [7:0] memoire6,
  output [7:0] memoire7,
  output [7:0] memoire8
);

  wire demultiplexer_1_out0, demultiplexer_1_out1, demultiplexer_1_out2, demultiplexer_1_out3,
       demultiplexer_1_out4, demultiplexer_1_out5, demultiplexer_1_out6, demultiplexer_1_out7;

  Demultiplexer #(.select(3)) demultiplexer_1 (
    .out0(demultiplexer_1_out0), .out1(demultiplexer_1_out1), .out2(demultiplexer_1_out2),
    .out3(demultiplexer_1_out3), .out4(demultiplexer_1_out4), .out5(demultiplexer_1_out5),
    .out6(demultiplexer_1_out6), .out7(demultiplexer_1_out7), .in(WE), .sel(right));
  Registre8bit registre8bit_1 (.D(Value), .WE(demultiplexer_1_out0), .out_3(memoire1));
  Registre8bit registre8bit_2 (.D(Value), .WE(demultiplexer_1_out1), .out_3(memoire2));
  Registre8bit registre8bit_3 (.D(Value), .WE(demultiplexer_1_out2), .out_3(memoire3));
  Registre8bit registre8bit_4 (.D(Value), .WE(demultiplexer_1_out3), .out_3(memoire4));
  Registre8bit registre8bit_5 (.D(Value), .WE(demultiplexer_1_out4), .out_3(memoire5));
  Registre8bit registre8bit_6 (.D(Value), .WE(demultiplexer_1_out5), .out_3(memoire6));
  Registre8bit registre8bit_7 (.D(Value), .WE(demultiplexer_1_out6), .out_3(memoire7));
  Registre1bit registre1bit_1 (.D(Value), .WE(demultiplexer_1_out7), .out_3(memoire8));
endmodule

module decodeur (
  input  [23:0] instruction,
  output [2:0] typeOpe,
  output [2:0] OP,
  output [2:0] Rin1,
  output [2:0] Rin2,
  output [3:0] Void,
  output [2:0] Rout
);

  wire clock_1_out;
  wire [23:3] register_1_q;

  Register #(.width(24)) register_1 (
    .D(instruction), .clk(clock_1_out),
    .Q({register_1_q[23:22], typeOpe, OP, register_1_q[15], Rin1, register_1_q[11], Rin2, Void, register_1_q[3], Rout}));  // open: en, clr
  Clock clock_1 (.out(clock_1_out));
  // NoConnect on register_1_q[22]
  // NoConnect on register_1_q[23]
endmodule

module RAMinstructions (
  input  [23:0] adresse,
  input  WE,
  input  OE,
  input  [23:0] entrer,
  output [23:0] sortie
);

  wire clock_1_out;

  Clock clock_1 (.out(clock_1_out));
  RAM #(.addrWidth(24), .dataWidth(24)) ram_1 (
    .addr(adresse), .we(WE), .oe(OE), .clk(clock_1_out), .din(entrer), .dout(sortie));
endmodule

module RAMdonnees (
  input  [7:0] adresse,
  input  WE,
  input  OE,
  input  [7:0] entre,
  output [7:0] sortie
);

  wire clock_1_out;

  Clock clock_1 (.out(clock_1_out));
  RAM ram_1 (.addr(adresse), .we(WE), .oe(OE), .clk(clock_1_out), .din(entre), .dout(sortie));
endmodule

module ProgramCounter (
  input  [23:0] instruction,
  output [23:0] out_2
);

  wire clock_1_out;

  Register #(.width(24)) register_1 (.D(instruction), .en(1'b1), .clk(clock_1_out), .Q(out_2));  // open: clr
  Clock clock_1 (.out(clock_1_out));
endmodule

module FETCH (
  input  [23:0] instruction,
  output [23:0] out_2
);

  wire clock_1_out;

  Register #(.width(24)) register_1 (.D(instruction), .en(1'b1), .clk(clock_1_out), .Q(out_2));  // open: clr
  Clock clock_1 (.out(clock_1_out));
endmodule

module CheminDonnees (
  output [23:0] out_1
);

  wire [23:0] adder_1_out, programcounter_1_out_2, raminstructions_1_sortie, undriven;

  Adder #(.width(24)) adder_1 (.a(programcounter_1_out_2), .b(24'h1), .out(adder_1_out));  // open: cin, cout
  ProgramCounter programcounter_1 (.instruction(adder_1_out), .out_2(programcounter_1_out_2));
  // NoConnect on undriven
  RAMinstructions raminstructions_1 (
    .adresse(programcounter_1_out_2), .WE(1'b0), .OE(1'b1), .entrer(undriven),
    .sortie(raminstructions_1_sortie));
  FETCH fetch_1 (.instruction(raminstructions_1_sortie), .out_2(out_1));
endmodule

module LOAD (
  input  [7:0] ALU,
  input  [7:0] RAM,
  input  [7:0] CNST8,
  input  [2:0] instruction,
  output [7:0] REG_IN
);

  Multiplexer #(.select(3), .width(8)) multiplexer_1 (
    .in0(ALU), .in3(RAM), .in6(CNST8), .out(REG_IN), .sel(instruction));  // open: in1, in2, in4, in5, in7
endmodule
